// Logisim project CS240_Chowdhury_Arunavo.circ as structural Verilog: 10 circuits, main circuit main
module main (
  input  A3,
  input  A2,
  input  A1,
  input  A0,
  input  B3,
  input  B2,
  input  B1,
  input  B0,
  input  COntrol,
  output out_10,
  output out_11,
  output out_12
);

  _2s_complement_control u_2s_complement_control_1 (
    .A3(A3), .A2(A2), .A1(A1), .A0(A0), .C(COntrol), .B3(B3), .B2(B2), .B1(B1), .B0(B0), .out_10(out_10),
    .out_11(out_11), .out_12(out_12));
endmodule

module HalfAdder (
  input  in_1,
  input  in_2,
  output out_3,
  output out_4
);

  and and_1 (out_4, in_1, in_2);
  xor xor_1 (out_3, in_1, in_2);
endmodule

module _4BitEqual (
  input  in_1,
  input  in_2,
  input  in_3,
  input  in_4,
  input  in_5,
  input  in_6,
  input  in_7,
  input  in_8,
  output out_9
);

  wire not_1_out, not_2_out, not_3_out, not_4_out, xor_1_out, xor_2_out, xor_3_out, xor_4_out;

  xor xor_1 (xor_1_out, in_1, in_5);
  not not_1 (not_1_out, xor_1_out);
  xor xor_2 (xor_2_out, in_6, in_2);
  not not_2 (not_2_out, xor_2_out);
  and and_1 (out_9, not_1_out, not_2_out, not_3_out, not_4_out);
  xor xor_3 (xor_3_out, in_3, in_7);
  not not_3 (not_3_out, xor_3_out);
  xor xor_4 (xor_4_out, in_4, in_8);
  not not_4 (not_4_out, xor_4_out);
endmodule

module TwosComplement (
  input  in_1,
  input  in_2,
  input  in_3,
  input  in_4,
  input  in_5,
  output out_6,
  output out_7,
  output out_8,
  output out_9,
  output out_10
);

  wire halfadder_2_out_4, halfadder_3_out_4, halfadder_4_out_4, xor_1_out, xor_2_out, xor_3_out, xor_4_out;

  xor xor_1 (xor_1_out, in_1, in_5);
  HalfAdder halfadder_1 (.in_1(halfadder_2_out_4), .in_2(xor_1_out), .out_3(out_7), .out_4(out_6));
  xor xor_2 (xor_2_out, in_2, in_5);
  HalfAdder halfadder_2 (.in_1(halfadder_3_out_4), .in_2(xor_2_out), .out_3(out_8), .out_4(halfadder_2_out_4));
  xor xor_3 (xor_3_out, in_3, in_5);
  HalfAdder halfadder_3 (.in_1(halfadder_4_out_4), .in_2(xor_3_out), .out_3(out_9), .out_4(halfadder_3_out_4));
  xor xor_4 (xor_4_out, in_4, in_5);
  HalfAdder halfadder_4 (.in_1(in_5), .in_2(xor_4_out), .out_3(out_10), .out_4(halfadder_4_out_4));
endmodule

module _4BitA_B (
  input  in_1,
  input  in_2,
  input  in_3,
  input  in_4,
  input  in_5,
  input  in_6,
  input  in_7,
  input  in_8,
  output out_9
);

  wire and_1_out, and_2_out, and_3_out, and_4_out, not_1_out, not_2_out, not_3_out, not_4_out, not_5_out,
       not_6_out, not_7_out, xor_1_out, xor_2_out, xor_3_out;

  not not_1 (not_1_out, in_5);
  and and_1 (and_1_out, in_1, not_1_out);
  xor xor_1 (xor_1_out, in_1, in_5);
  not not_2 (not_2_out, in_6);
  not not_3 (not_3_out, xor_1_out);
  and and_2 (and_2_out, in_2, not_3_out, not_2_out);
  or or_1 (out_9, and_1_out, and_2_out, and_3_out, and_4_out);
  xor xor_2 (xor_2_out, in_2, in_6);
  not not_4 (not_4_out, xor_2_out);
  and and_3 (and_3_out, not_3_out, in_3, not_4_out, not_5_out);
  not not_5 (not_5_out, in_7);
  and and_4 (and_4_out, not_3_out, not_4_out, not_6_out, in_4, not_7_out);
  xor xor_3 (xor_3_out, in_3, in_7);
  not not_6 (not_6_out, xor_3_out);
  not not_7 (not_7_out, in_8);
endmodule

module _4BitA_B_2 (
  input  in_1,
  input  in_2,
  input  in_3,
  input  in_4,
  input  in_5,
  input  in_6,
  input  in_7,
  input  in_8,
  output out_9
);

  wire and_1_out, and_2_out, and_3_out, and_4_out, not_1_out, not_2_out, not_3_out, not_4_out, not_5_out,
       not_6_out, not_7_out, xor_1_out, xor_2_out, xor_3_out;

  not not_1 (not_1_out, in_1);
  and and_1 (and_1_out, not_1_out, in_5);
  not not_2 (not_2_out, in_2);
  xor xor_1 (xor_1_out, in_1, in_5);
  not not_3 (not_3_out, xor_1_out);
  and and_2 (and_2_out, not_2_out, not_3_out, in_6);
  or or_1 (out_9, and_1_out, and_2_out, and_3_out, and_4_out);
  xor xor_2 (xor_2_out, in_2, in_6);
  not not_4 (not_4_out, in_3);
  not not_5 (not_5_out, xor_2_out);
  and and_3 (and_3_out, not_3_out, not_4_out, not_5_out, in_7);
  xor xor_3 (xor_3_out, in_3, in_7);
  not not_6 (not_6_out, xor_3_out);
  and and_4 (and_4_out, not_3_out, not_5_out, not_6_out, not_7_out, in_8);
  not not_7 (not_7_out, in_4);
endmodule

module Mux (
  input  _4,
  input  _3,
  input  _2,
  input  _1,
  output out_5
);

  wire and_1_out, and_2_out;

  and and_1 (and_1_out, _4, _3);
  and and_2 (and_2_out, _2, _1);
  xor xor_1 (out_5, and_1_out, and_2_out);
endmodule

module Unsigned_Comparator (
  input  A3,
  input  A2,
  input  A1,
  input  A0,
  input  B3,
  input  B2,
  input  B1,
  input  B0,
  output out_9,
  output out_10,
  output out_11
);

  _4BitA_B_2 u_4bita_b_1 (
    .in_1(A3), .in_2(A2), .in_3(A1), .in_4(A0), .in_5(B3), .in_6(B2), .in_7(B1), .in_8(B0), .out_9(out_10));
  _4BitEqual u_4bitequal_1 (
    .in_1(A3), .in_2(A2), .in_3(A1), .in_4(A0), .in_5(B3), .in_6(B2), .in_7(B1), .in_8(B0), .out_9(out_11));
  _4BitA_B u_4bita_b_2 (
    .in_1(A3), .in_2(A2), .in_3(A1), .in_4(A0), .in_5(B3), .in_6(B2), .in_7(B1), .in_8(B0), .out_9(out_9));
endmodule

module _2s_complement_comparator (
  input  A3,
  input  A2,
  input  A1,
  input  A0,
  input  B3,
  input  B2,
  input  B1,
  input  B0,
  output out_9,
  output out_10,
  output out_11
);

  wire mux_1_out_5, mux_2_out_5, not_1_out, not_2_out, not_3_out, not_4_out, xor_1_out;

  _4BitA_B_2 u_4bita_b_1 (
    .in_1(mux_1_out_5), .in_2(A2), .in_3(A1), .in_4(A0), .in_5(mux_2_out_5), .in_6(B2), .in_7(B1), .in_8(B0),
    .out_9(out_9));
  xor xor_1 (xor_1_out, B3, A3);
  _4BitEqual u_4bitequal_1 (
    .in_1(mux_1_out_5), .in_2(A2), .in_3(A1), .in_4(A0), .in_5(mux_2_out_5), .in_6(B2), .in_7(B1), .in_8(B0),
    .out_9(out_10));
  not not_1 (not_1_out, xor_1_out);
  not not_2 (not_2_out, A3);
  not not_3 (not_3_out, xor_1_out);
  not not_4 (not_4_out, B3);
  Mux mux_1 (._4(A3), ._3(not_1_out), ._2(not_2_out), ._1(xor_1_out), .out_5(mux_1_out_5));
  Mux mux_2 (._4(B3), ._3(not_3_out), ._2(xor_1_out), ._1(not_4_out), .out_5(mux_2_out_5));
  _4BitA_B u_4bita_b_2 (
    .in_1(mux_1_out_5), .in_2(A2), .in_3(A1), .in_4(A0), .in_5(mux_2_out_5), .in_6(B2), .in_7(B1), .in_8(B0),
    .out_9(out_11));
endmodule

module _2s_complement_control (
  input  A3,
  input  A2,
  input  A1,
  input  A0,
  input  B3,
  input  B2,
  input  B1,
  input  B0,
  input  C,
  output out_10,
  output out_11,
  output out_12
);

  wire n2s_complement_comparator_1_out_9, n2s_complement_comparator_1_out_10,
       n2s_complement_comparator_1_out_11, not_1_out, not_2_out, not_3_out, unsigned_comparator_1_out_9,
       unsigned_comparator_1_out_10, unsigned_comparator_1_out_11;

  Unsigned_Comparator unsigned_comparator_1 (
    .A3(A3), .A2(A2), .A1(A1), .A0(A0), .B3(B3), .B2(B2), .B1(B1), .B0(B0),
    .out_10(unsigned_comparator_1_out_10), .out_11(unsigned_comparator_1_out_11),
    .out_9(unsigned_comparator_1_out_9));
  not not_1 (not_1_out, C);
  Mux mux_1 (
    ._4(n2s_complement_comparator_1_out_9), ._3(C), ._2(unsigned_comparator_1_out_10), ._1(not_1_out),
    .out_5(out_10));
  not not_2 (not_2_out, C);
  Mux mux_2 (
    ._4(n2s_complement_comparator_1_out_10), ._3(C), ._2(unsigned_comparator_1_out_11), ._1(not_2_out),
    .out_5(out_11));
  _2s_complement_comparator u_2s_complement_comparator_1 (
    .A3(A3), .A2(A2), .A1(A1), .A0(A0), .B3(B3), .B2(B2), .B1(B1), .B0(B0),
    .out_9(n2s_complement_comparator_1_out_9), .out_10(n2s_complement_comparator_1_out_10),
    .out_11(n2s_complement_comparator_1_out_11));
  not not_3 (not_3_out, C);
  Mux mux_3 (
    ._4(n2s_complement_comparator_1_out_11), ._3(C), ._2(unsigned_comparator_1_out_9), ._1(not_3_out),
    .out_5(out_12));
endmodule
